# Fritzing sketch schema (saved by Fritzing 0.9.4)

parts:
  U5 = NodeMCU V3.0 CH340G
  KF-1 = KF-301 Relay [package=THT]
  WATER_PUMP1 = water pump/motor  # not connected
  Part2 = Soil Moisture Sensor
  Part3 = I2C level shifter bidirectional
  Part4 = OpAmp Breakout
  U7 = POT [package=pot_mammoth]  # not connected
  VCC1 = Battery block 9V  # not connected
  Grove1 = Grove OLED 128x96

nets:
  N1: U5.D1, Grove1.SCL
  N2: U5.D2, Grove1.SDA
  3V3: U5.3V3, Part3.LV, Grove1.VCC
  GND: U5.GND, Part2.GND, Grove1.GND
  N3: U5.D5, Part3.LV3
  N4: U5.D6, Part3.LV4
  N5: KF-1.signal, Part3.HV3
  N6: KF-1.power, Part2.VCC, Part3.HV
  N7: KF-1.ground, Part3.GND
  N8: KF-1.C, Part4.M-
  N9: Part2.SIG, Part3.HV4

custom parts:
  NodeMCU V3.0 CH340G: NodeMcu V3 Lua WIFI Development Board
  KF-301 Relay: KF-301
  water pump/motor: WATER PUMP BY ARDUBLOCKTR
  OpAmp Breakout: Description: This is a simple Op Amp breakout board, set up as a 2-stage amplifier with a gain of 100 (gain of 10 for each stage). The on-board trim pot sets the signal level between the stages, not the feedback path. The bandwidth is set to 15.9kHz by a pair of feedback capacitors, or over 100kHz with the caps removed. The LMV358 opamp can source up to 160mA and works well as a low impedance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
